// Logisim project Calculator.circ as structural Verilog: 3 circuits, main circuit main
module main (
  input  in_1,
  input  in_2,
  input  in_3,
  input  in_4,
  input  in_5,
  input  in_6,
  input  in_7,
  input  in_8
);

  wire multiplier_1_w, multiplier_1_x, multiplier_1_y, multiplier_1_z, n7448_1_p10, n7448_1_p11, n7448_1_p12,
       n7448_1_p13, n7448_1_p14, n7448_1_p15, n7448_1_p16, n74157_1_p4, n74157_1_p7, n74157_1_p13,
       n74157_1_p16, n74157_2_p3, n74157_2_p4, n74157_2_p6, n74157_2_p7, n74157_2_p12, n74157_2_p13,
       n74157_2_p15, n74157_2_p16, n74157_3_p2, n74157_3_p5, n74157_3_p11, n74157_3_p14, remainder_1_y,
       remainder_1_z, remainder_2_y, remainder_2_z;

  Remainder remainder_1 (
    .A(in_1), .B(in_2), .C(in_3), .D(in_4), .E(in_5), .F(in_6), .Y(remainder_1_y), .Z(remainder_1_z));  // open: N
  Multiplier multiplier_1 (
    .A(in_1), .B(in_2), .C(in_3), .D(in_4), .E(in_5), .F(in_6), .W(multiplier_1_w), .X(multiplier_1_x),
    .Y(multiplier_1_y), .Z(multiplier_1_z));  // open: N
  // _74157 74157_1: pin names not known; wires that end beside it: in_7, multiplier_1_z, remainder_1_z, n74157_1_p4, multiplier_1_y, remainder_1_y, n74157_1_p7, 1'b0, 1'b1, 1'b0, multiplier_1_x, 1'b0, n74157_1_p13, multiplier_1_w, 1'b0, n74157_1_p16
  Remainder remainder_2 (
    .A(in_1), .B(in_2), .C(in_3), .D(in_4), .E(in_5), .F(in_6), .Y(remainder_2_y), .Z(remainder_2_z));  // open: N
  // _74157 74157_2: pin names not known; wires that end beside it: in_8, n74157_1_p4, n74157_2_p3, n74157_2_p4, n74157_1_p7, n74157_2_p6, n74157_2_p7, 1'b0, 1'b1, 1'b0, n74157_1_p13, n74157_2_p12, n74157_2_p13, n74157_1_p16, n74157_2_p15, n74157_2_p16
  // _74157 74157_3: pin names not known; wires that end beside it: in_7, n74157_3_p2, remainder_2_z, n74157_2_p3, n74157_3_p5, remainder_2_y, n74157_2_p6, 1'b0, 1'b1, 1'b0, n74157_3_p11, 1'b0, n74157_2_p12, n74157_3_p14, 1'b0, n74157_2_p15
  Multiplier multiplier_2 (
    .A(in_1), .B(in_2), .C(in_3), .D(in_4), .E(in_5), .F(in_6), .W(n74157_3_p14), .X(n74157_3_p11),
    .Y(n74157_3_p5), .Z(n74157_3_p2));  // open: N
  // _7448 7448_1: pin names not known; wires that end beside it: n74157_2_p7, n74157_2_p13, 1'b1, 1'b1, 1'b1, n74157_2_p16, n74157_2_p4, 1'b0, 1'b1, n7448_1_p10, n7448_1_p11, n7448_1_p12, n7448_1_p13, n7448_1_p14, n7448_1_p15, n7448_1_p16
  _7_Segment_Display u_7_segment_display_1 (
    .g(n7448_1_p11), .f(n7448_1_p10), .a(n7448_1_p12), .b(n7448_1_p13), .e(n7448_1_p16), .d(n7448_1_p15),
    .c(n7448_1_p14));  // open: dp
  _7_Segment_Display u_7_segment_display_2 ();  // open: g, f, a, b, e, d, c, dp
endmodule

module Remainder (
  input  A,
  input  B,
  input  C,
  input  D,
  input  E,
  input  F,
  output N,
  output Y,
  output Z
);

  wire n7404_1_p2, n7404_1_p9, n7404_1_p11, n7408_1_p3, n7408_1_p6, n7408_1_p8, n7408_1_p10, n7408_1_p11,
       n7408_1_p12, n7408_2_p9;

  // _7408 7408_1: pin names not known; wires that end beside it: 1'b0, Y, n7408_1_p3, n7408_1_p3, F, n7408_1_p6, E, n7408_1_p8, n7408_1_p6, n7408_1_p10, n7408_1_p11, n7408_1_p12, B, 1'b1
  // _7404 7404_1: pin names not known; wires that end beside it: 1'b0, n7404_1_p2, n7408_1_p8, n7408_1_p12, n7408_1_p11, Y, C, n7408_1_p10, n7404_1_p9, Z, n7404_1_p11, 1'b1
  // _7408 7408_2: pin names not known; wires that end beside it: 1'b0, N, n7404_1_p11, A, B, n7404_1_p2, F, Z, n7408_2_p9, n7404_1_p9, C, n7408_2_p9, D, E, 1'b1
endmodule

module Multiplier (
  input  A,
  input  B,
  input  C,
  input  D,
  input  E,
  input  F,
  output N,
  output W,
  output X,
  output Y,
  output Z
);

  wire n7408_1_p3, n7408_1_p4, n7408_1_p5, n7408_1_p7;

  // _7408 7408_1: pin names not known; wires that end beside it: 1'b0, 1'b1, n7408_1_p3, n7408_1_p4, n7408_1_p5, n7408_1_p5, n7408_1_p7, W
  // _7408 7408_2: pin names not known; wires that end beside it: 1'b1, B, C, E, E, n7408_1_p7, n7408_1_p3, B, C, F, F, n7408_1_p4, Z, 1'b0
  // _7486 7486_1: pin names not known; wires that end beside it: n7408_1_p3, n7408_1_p4, Y, n7408_1_p5, n7408_1_p7, X, 1'b0, 1'b1, A, D, N
endmodule
